# Fritzing sketch Connection (saved by Fritzing 0.9.6b)

parts:
  J1 = STM32 Nucleo boards
  J2 = Basic Servo
  Componente1 = Soil Moisture Sensor
  DHT1 = DHT11 Humitidy and Temperature Sensor
  KY-1 = Keyes Relay [package=THT]
  Water_level_sensor = Water Level Sensor

nets:
  N1: J1.A0, Componente1.SIG
  N2: J1.A1, Water_level_sensor.SIG
  GND: J1.GND, J2.gnd, Componente1.GND
  N3: J1.D2, DHT1.DATA
  N4: J1.D3_PWM, J2.pulse
  N5: J1.D5_PWM, Water_level_sensor.VCC
  N6: J1.D7, KY-1.signal
  VCC: J1.5V, J2.vcc, Componente1.VCC

custom parts:
  DHT11 Humitidy and Temperature Sensor: DHT11 Humidity and Temperature Sensor
  Keyes Relay: The Keyes 5V relay module is suitable for SCM development, home appliance control. It uses a 5V~12V TIL control signal which can control DC / AC signal.
  Water Level Sensor: A water level sensor. This sensor operates at 3V to 5V. The Sig (signal) pin outputs an analogue signal that is in proportion to the amount of water in contact with the sensor.
